# Fritzing sketch brainstorm (saved by Fritzing 0.9.3b)
circuit board: 8.46667cm x 5.64444cm
breadboards: 2

parts:
  IC1 = IC, DIP package, 16 pins [chip_label=74LS191 part_number=74LS191]
  IC2 = IC, DIP package, 16 pins [chip_label=74LS191 part_number=74LS191]
  IC3 = IC, DIP package, 16 pins [chip_label=74LS191 part_number=74LS191]
  IC4 = IC, DIP package, 16 pins [chip_label=74LS191 part_number=74LS191]
  IC6 = IC, DIP package, 16 pins [chip_label=74LS245 part_number=74LS257]
  IC5 = IC, DIP package, 28 pins [chip_label=AT28C64A]
  J1 = female pin header, 8 pins [form="♀ (female)"]

nets:
  N1: IC1.pin1, IC1.pin4, IC1.pin8, IC1.pin9, IC1.pin10, IC1.pin15, IC2.pin1, IC2.pin4, IC2.pin8, IC2.pin9, IC2.pin10, IC2.pin15, IC3.pin1, IC3.pin4, IC3.pin8, IC3.pin9, IC3.pin10, IC3.pin15, IC4.pin1, IC4.pin4, IC4.pin8, IC4.pin9, IC4.pin10, IC4.pin15, IC6.pin8, IC6.pin15, IC5.pin14, IC5.pin20, IC5.pin28
  N2: IC1.pin2, IC5.pin21
  N3: IC1.pin3, IC5.pin23
  N4: IC1.pin6, IC5.pin24
  N5: IC1.pin7, IC5.pin25
  N6: IC1.pin11, IC2.pin11, IC3.pin11, IC4.pin11
  N7: IC1.pin13, IC2.pin14
  N8: IC1.pin16, IC2.pin16, IC3.pin16, IC4.pin16, IC6.pin16
  N9: IC2.pin2, IC5.pin5
  N10: IC2.pin3, IC5.pin4
  N11: IC2.pin6, IC5.pin3
  N12: IC2.pin7, IC5.pin2
  N13: IC2.pin13, IC3.pin14
  N14: IC3.pin2, IC5.pin9
  N15: IC3.pin3, IC5.pin8
  N16: IC3.pin6, IC5.pin7
  N17: IC3.pin7, IC5.pin6
  N18: IC3.pin13, IC4.pin14
  N19: IC4.pin7, IC5.pin10
  N20: IC6.pin2, IC5.pin17, J1.pin6
  N21: IC6.pin3, IC5.pin18, J1.pin5
  N22: IC6.pin5, IC6.pin6, IC5.pin19, J1.pin7, J1.pin8
  N23: IC6.pin10, IC5.pin15, J1.pin4
  N24: IC6.pin11, IC5.pin11, J1.pin3
  N25: IC6.pin13, IC5.pin12, J1.pin2
  N26: IC6.pin14, IC5.pin13, J1.pin1
