// Logisim project non-bf computer.circ as structural Verilog: 2 circuits, main circuit main
module main (
);

  wire [3:0] undriven, undriven_2, undriven_3;
  wire [7:0] ram_1_data, ram_2_data, rom_1_data, rom_2_data;
  wire [15:0] counter_1_q;

  Counter #(.width(16), .max('hffff)) counter_1 (.Q(counter_1_q));  // open: load, D, count, carry, clk, clr
  ROM #(.addrWidth(15)) rom_1 (.addr(counter_1_q[15:1]), .data(rom_1_data));  // open: sel
  ROM #(.addrWidth(15)) rom_2 (.addr(counter_1_q[15:1]), .data(rom_2_data));  // open: sel
  RAM #(.addrWidth(4)) ram_1 (.addr(undriven), .data(ram_1_data));  // open: sel, clk, ld, clr
  RAM #(.addrWidth(4)) ram_2 (.addr(undriven_2), .data(ram_2_data));  // open: sel, clk, ld, clr
  ALU alu_1 (.A0_8(ram_1_data), .B0_8(ram_2_data), .S0_3(undriven_3));  // open: Cn, M, F0_8, Cn___4, A_B, G, P

  // Notes on the sheet:
  //   Instructions
  //   LoadConst Const -> RegA
  //   Add RegA + RegB -> RegC
  //   Sub RegA + RegB -> RegC
  //   AND RegA && RegB -> RegC
  //   OR RegA || RegB -> RegC
  //   NOT RegA -> RegC
  //   ROTATE RegA, #bits
  //   SHIFT RegA, #bits
  //   JUMP RegA>0, Address
  //   Load AddressRegA AddressRegB -> RegA
  //   Store RegA -> AddressRegA AddressRegB
  //   Registers
  //   0s
  //   1s
  //   6x Other Reg
  //   8 data width, 16 bit address width
  //   Instruction
  //   0000 - 000- 000- 000
  //   OPCode    RegA    RegB    RegC
endmodule

module ALU (
  input  [7:0] A0_8,
  input  [7:0] B0_8,
  input  [3:0] S0_3,
  input  Cn,
  input  M,
  output [7:0] F0_8,
  output Cn___4,
  output A_B,
  output G,
  output P
);


  assign A_B = 1'b0;
  assign Cn___4 = 1'b0;
  assign F0_8 = {8{1'b0}};
  assign G = 1'b0;
  assign P = 1'b0;
endmodule
